# Fritzing sketch project_schematic (saved by Fritzing 0.9.4)
circuit board: 12.5802cm x 6.53466cm
breadboards: 1

parts:
  OUT-Pump = DC Motor
  Arduino = Arduino Uno (Rev3)
  Fan_motor = DC Motor
  Relay_for_OUT-pump = RELAY [package=relay-g5q]
  Relay_for_IN-pump = RELAY [package=relay-g5q]
  MQ-135_Gas_sensor = mystery part, 3 pins [chip_label=GAS]
  YF-S201_Flow_sensor_IN = mystery part, 3 pins [chip_label=FLOW]
  YF-S201_Flow_sensor_OUT = mystery part, 3 pins [chip_label=FLOW]
  Power_12V = Power plug
  IN-Pump = DC Motor
  DHT11 = mystery part, 3 pins [chip_label=DHT11]
  Water_level_sensor = mystery part, 3 pins [chip_label="W. lvl"]
  2-channel_Motor_Driver = Motor Driver 1A Dual TB6612FNG

nets:
  N1: OUT-Pump.pin_1, Relay_for_OUT-pump.NO
  GND: OUT-Pump.pin_2, Arduino.GND, Relay_for_OUT-pump.COIL2, Relay_for_IN-pump.COIL2, MQ-135_Gas_sensor.pin1, YF-S201_Flow_sensor_IN.pin1, YF-S201_Flow_sensor_OUT.pin1, Power_12V.GND, IN-Pump.pin_2, DHT11.pin1, Water_level_sensor.pin1, 2-channel_Motor_Driver.GND
  N2: Arduino.A0, YF-S201_Flow_sensor_OUT.pin3
  N3: Arduino.A1, YF-S201_Flow_sensor_IN.pin3
  N4: Arduino.A2, MQ-135_Gas_sensor.pin3
  Arduino - IN-Pump: Arduino.D12/MISO, Relay_for_IN-pump.COIL1
  Arduino - OUT-Pump: Arduino.D13/SCK, Relay_for_OUT-pump.COIL1
  N5: Arduino.D2, Water_level_sensor.pin3
  Arduino - Motor Driver pin1: Arduino.D3_PWM, 2-channel_Motor_Driver.BIN1
  N6: Arduino.D4, DHT11.pin3
  Arduino - Motor Driver pin2: Arduino.D5_PWM, 2-channel_Motor_Driver.BIN2
  Arduino - Motor driver PWM: Arduino.D6_PWM, 2-channel_Motor_Driver.PWMB
  5V: Arduino.5V, MQ-135_Gas_sensor.pin2, YF-S201_Flow_sensor_IN.pin2, YF-S201_Flow_sensor_OUT.pin2, DHT11.pin2, 2-channel_Motor_Driver.VCC, 2-channel_Motor_Driver.STBY
  N7: Fan_motor.pin_1, 2-channel_Motor_Driver.B01
  N8: Fan_motor.pin_2, 2-channel_Motor_Driver.B02
  12V: Relay_for_OUT-pump.MAIN, Relay_for_IN-pump.MAIN, Power_12V.VCC, 2-channel_Motor_Driver.VM
  N9: Relay_for_IN-pump.NO, IN-Pump.pin_1

notes:
  Левый мотор - помпа откачки из жилого бокса
  Правый - в жилой бокс
  Вентилятор
